# Fritzing sketch TTY Connector (saved by Fritzing 0.9.6b)

parts:
  Mod1 = Raspberry Pi 4B
  USBTTL1 = USB TTL Serial Cable

nets:
  GND: Mod1.GND, USBTTL1.GND
  N1: Mod1.GPIO14, USBTTL1.RX
  N2: Mod1.GPIO15, USBTTL1.TX
